# Fritzing sketch IMU hookup (saved by Fritzing 0.8.7b)
breadboards: 1

parts:
  IMU1 = Adafruit 10-DOF IMU Breakout
  Part1 = Arduino Uno (Rev3)

nets:
  VIN: IMU1.VIN, Part1.5V
  GND: IMU1.GND, Part1.GND
  N1: IMU1.SCL, Part1.A5/SCL
  N2: IMU1.SDA, Part1.A4/SDA
