# Fritzing sketch noninverting amplifier (saved by Fritzing 0.8.7b)
breadboards: 1

parts:
  IC1 = IC, DIP package, 14 pins [chip_label=IC]
  C1 = Ceramic Capacitor [capacitance=100nF voltage=50V package="100 mil [THT, multilayer]"]
  R1 = Rotary Potentiometer (Small) [maximum_resistance=100kΩ package=THT]
  R2 = Resistor [tolerance=±5% resistance=10k package=THT]
  R3 = Resistor [tolerance=±5% resistance=10k package=THT]

nets:
  N1: IC1.pin4, C1.0, R1.leg2
  N2: IC1.pin5, R1.wiper
  N3: IC1.pin6, R2.Pin_1, R3.Pin_0
  N4: IC1.pin7, R2.Pin_0
  N5: IC1.pin11, C1.1, R1.leg1, R3.Pin_1
