# Fritzing sketch temp-sensor-hookup (saved by Fritzing 0.8.7b)

parts:
  U1 = TMP36 [package=to-92-kit]
  Part1 = Arduino Uno (Rev3)

nets:
  VCC: U1.VCC, Part1.5V
  N1: U1.VOUT, Part1.A0
  GND: U1.GND, Part1.GND
