# Fritzing sketch voltage-follower (saved by Fritzing 0.8.7b)
breadboards: 1

parts:
  IC1 = IC, DIP package, 14 pins [chip_label=IC]
  C1 = Ceramic Capacitor [capacitance=100nF voltage=50V package="100 mil [THT, multilayer]"]

nets:
  N1: IC1.pin4, C1.0
  N2: IC1.pin11, C1.1
